# Fritzing sketch Machine_Vision (saved by Fritzing 0.9.3b)
breadboards: 2

parts:
  Disp1 = LBT2088AH [part_number=LBT2088AH]
  Part1 = Arduino Ethernet Shield (Rev3)

nets:
  N1: Disp1.pin1, Part1.PWM_D6
  N2: Disp1.pin2, Part1.D8
  N3: Disp1.pin_3, Part1.PWM_D11
  N4: Disp1.pin_4, Part1.SPI/D12
  N5: Disp1.pin_5, Part1.PWM_D9
  N6: Disp1.pin_6, Part1.A0
  N7: Disp1.pin_7, Part1.D7
  N8: Disp1.pin_8, Part1.SDCS
  N9: Disp1.pin_9, Part1.D2
  N10: Disp1.pin_10, Part1.SPI/D13
  N11: Disp1.pin_11, Part1.A1
  N12: Disp1.pin_12, Part1.PWM_D5
  N13: Disp1.pin_13, Part1.ETH_CS
  N14: Disp1.pin_14, Part1.PWM_D3
  N15: Disp1.pin_15, Part1.A2
  N16: Disp1.pin_16, Part1.A3

notes:
  Row - violet
  Column - Yellow
